// Logisim project 24_bit_cpu.circ as structural Verilog: 9 circuits, main circuit CPU_24Bit
module CPU_24Bit (
);

  wire alu_24bit_1_flag_carry, alu_24bit_1_flag_zero, and_1_out, clock_1_out,
       cpu_firmwarechip_1_enable_ram_output, cpu_firmwarechip_1_enable_source,
       cpu_firmwarechip_1_expansionport_load, cpu_firmwarechip_1_expansionport_store,
       cpu_firmwarechip_1_halt, cpu_firmwarechip_1_pc_enable, cpu_firmwarechip_1_ram_read,
       cpu_firmwarechip_1_ram_write, cpu_firmwarechip_1_register_load, cpu_firmwarechip_1_register_store,
       Reset_RAM_out, Reset_System_out;
  wire [0:0] cpu_firmwarechip_1_ram_address_load;
  wire [1:0] alu_24bit_1_flag_compare, register_mapper_1_acc, register_mapper_1_pc, register_mapper_1_rea,
       register_mapper_1_reb, register_mapper_1_rep, register_mapper_1_req, register_mapper_1_rer,
       register_mapper_1_res, register_mapper_1_ret, register_mapper_1_reu, register_mapper_1_rev,
       register_mapper_1_rew, register_mapper_1_rex, register_mapper_1_rey, register_mapper_1_rez,
       register_mapper_1_sp;
  wire [2:0] cpu_firmwarechip_1_alu_operation, cpu_firmwarechip_1_expansionport_addreess;
  wire [3:0] cpu_firmwarechip_1_destination_register, cpu_firmwarechip_1_register_address,
       cpu_firmwarechip_1_source_register, or_1_out;
  wire [23:0] alu_24bit_1_acc, ram_1_dout, register_24bit_1_output_data, register_24bit_8_output_display,
       register_24bit_9_output_display, register_24bit_16_output_data;

  and and_1 (and_1_out, ~Reset_System_out, ~cpu_firmwarechip_1_halt, clock_1_out);  // AND_Gate
  Clock clock_1 (.out(clock_1_out));
  CPU_FirmwareChip cpu_firmwarechip_1 (
    .Flag_Compare(alu_24bit_1_flag_compare), .Flag_Zero(alu_24bit_1_flag_zero),
    .Flag_Carry(alu_24bit_1_flag_carry), .Data(register_24bit_1_output_data), .Clock(and_1_out),
    .Clear(Reset_System_out), .Register_Address(cpu_firmwarechip_1_register_address),
    .Register_Load(cpu_firmwarechip_1_register_load), .Register_Store(cpu_firmwarechip_1_register_store),
    .PC_Enable(cpu_firmwarechip_1_pc_enable), .RAM_Address_Load(cpu_firmwarechip_1_ram_address_load[0]),
    .RAM_Read(cpu_firmwarechip_1_ram_read), .RAM_Write(cpu_firmwarechip_1_ram_write),
    .ExpansionPort_Addreess(cpu_firmwarechip_1_expansionport_addreess),
    .ExpansionPort_Store(cpu_firmwarechip_1_expansionport_store),
    .ExpansionPort_Load(cpu_firmwarechip_1_expansionport_load), .Halt(cpu_firmwarechip_1_halt),
    .ALU_Operation(cpu_firmwarechip_1_alu_operation),
    .Enable_RAM_Output(cpu_firmwarechip_1_enable_ram_output),
    .Enable_Source(cpu_firmwarechip_1_enable_source), .Source_Register(cpu_firmwarechip_1_source_register),
    .Destination_Register(cpu_firmwarechip_1_destination_register));  // open: Instruction_Read, out_19
  assign or_1_out = cpu_firmwarechip_1_destination_register | cpu_firmwarechip_1_register_address;  // OR_Gate or_1, 4 bits wide
  Register_24Bit register_24bit_1 (
    .Load_Store(register_mapper_1_sp), .Input_Data(register_24bit_1_output_data), .Clock(and_1_out),
    .Clear(Reset_System_out), .Output_Data(register_24bit_1_output_data));  // open: Output_Display
  ProgramCounter_24Bit programcounter_24bit_1 (
    .Clear(Reset_System_out), .Load(register_mapper_1_pc), .Enable(cpu_firmwarechip_1_pc_enable),
    .Clock(and_1_out), .Data(register_24bit_1_output_data), .Pointer(register_24bit_1_output_data));
  Register_Mapper register_mapper_1 (
    .Load(cpu_firmwarechip_1_register_load), .Store(cpu_firmwarechip_1_register_store),
    .Enable_Source(cpu_firmwarechip_1_enable_source), .Source(cpu_firmwarechip_1_source_register),
    .Address(or_1_out), .REP(register_mapper_1_rep), .SP(register_mapper_1_sp), .PC(register_mapper_1_pc),
    .REA(register_mapper_1_rea), .REB(register_mapper_1_reb), .ACC(register_mapper_1_acc),
    .REZ(register_mapper_1_rez), .REY(register_mapper_1_rey), .REX(register_mapper_1_rex),
    .REW(register_mapper_1_rew), .REV(register_mapper_1_rev), .REU(register_mapper_1_reu),
    .RET(register_mapper_1_ret), .RES(register_mapper_1_res), .RER(register_mapper_1_rer),
    .REQ(register_mapper_1_req));
  Register_24Bit register_24bit_2 (
    .Load_Store(register_mapper_1_rez), .Input_Data(register_24bit_1_output_data), .Clock(and_1_out),
    .Clear(Reset_System_out), .Output_Data(register_24bit_1_output_data));  // open: Output_Display
  Register_24Bit register_24bit_3 (
    .Load_Store(register_mapper_1_rey), .Input_Data(register_24bit_1_output_data), .Clock(and_1_out),
    .Clear(Reset_System_out), .Output_Data(register_24bit_1_output_data));  // open: Output_Display
  Register_24Bit register_24bit_4 (
    .Load_Store(register_mapper_1_rex), .Input_Data(register_24bit_1_output_data), .Clock(and_1_out),
    .Clear(Reset_System_out), .Output_Data(register_24bit_1_output_data));  // open: Output_Display
  Register_24Bit register_24bit_5 (
    .Load_Store(register_mapper_1_rew), .Input_Data(register_24bit_1_output_data), .Clock(and_1_out),
    .Clear(Reset_System_out), .Output_Data(register_24bit_1_output_data));  // open: Output_Display
  Register_24Bit register_24bit_6 (
    .Load_Store(register_mapper_1_rev), .Input_Data(register_24bit_1_output_data), .Clock(and_1_out),
    .Clear(Reset_System_out), .Output_Data(register_24bit_1_output_data));  // open: Output_Display
  Register_24Bit register_24bit_7 (
    .Load_Store(register_mapper_1_reu), .Input_Data(register_24bit_1_output_data), .Clock(and_1_out),
    .Clear(Reset_System_out), .Output_Data(register_24bit_1_output_data));  // open: Output_Display
  Register_24Bit register_24bit_8 (
    .Load_Store(register_mapper_1_rea), .Input_Data(register_24bit_1_output_data), .Clock(and_1_out),
    .Clear(Reset_System_out), .Output_Display(register_24bit_8_output_display),
    .Output_Data(register_24bit_1_output_data));
  Register_24Bit register_24bit_9 (
    .Load_Store(register_mapper_1_reb), .Input_Data(register_24bit_1_output_data), .Clock(and_1_out),
    .Clear(Reset_System_out), .Output_Display(register_24bit_9_output_display),
    .Output_Data(register_24bit_1_output_data));
  Register_24Bit register_24bit_10 (
    .Load_Store(register_mapper_1_ret), .Input_Data(register_24bit_1_output_data), .Clock(and_1_out),
    .Clear(Reset_System_out), .Output_Data(register_24bit_1_output_data));  // open: Output_Display
  Register_24Bit register_24bit_11 (
    .Load_Store(register_mapper_1_res), .Input_Data(register_24bit_1_output_data), .Clock(and_1_out),
    .Clear(Reset_System_out), .Output_Data(register_24bit_1_output_data));  // open: Output_Display
  Register_24Bit register_24bit_12 (
    .Load_Store(register_mapper_1_rer), .Input_Data(register_24bit_1_output_data), .Clock(and_1_out),
    .Clear(Reset_System_out), .Output_Data(register_24bit_1_output_data));  // open: Output_Display
  Register_24Bit register_24bit_13 (
    .Load_Store(register_mapper_1_req), .Input_Data(register_24bit_1_output_data), .Clock(and_1_out),
    .Clear(Reset_System_out), .Output_Data(register_24bit_1_output_data));  // open: Output_Display
  Register_24Bit register_24bit_14 (
    .Load_Store(register_mapper_1_rep), .Input_Data(register_24bit_1_output_data), .Clock(and_1_out),
    .Clear(Reset_System_out), .Output_Data(register_24bit_1_output_data));  // open: Output_Display
  Expansion_Mapper expansion_mapper_1 (
    .ExpansionPort_Address(cpu_firmwarechip_1_expansionport_addreess),
    .Store(cpu_firmwarechip_1_expansionport_store), .Load(cpu_firmwarechip_1_expansionport_load));  // open: EP0, EP1, EP2, EP3, EP4, EP5, EP6, EP7
  ALU_24Bit alu_24bit_1 (
    .SelectMode(cpu_firmwarechip_1_alu_operation), .A(register_24bit_8_output_display),
    .B(register_24bit_9_output_display), .Flag_Carry(alu_24bit_1_flag_carry),
    .Flag_Zero(alu_24bit_1_flag_zero), .ACC(alu_24bit_1_acc), .Flag_Compare(alu_24bit_1_flag_compare));
  Register_24Bit register_24bit_15 (
    .Load_Store(register_mapper_1_acc), .Input_Data(alu_24bit_1_acc), .Clock(and_1_out),
    .Clear(Reset_System_out), .Output_Data(register_24bit_1_output_data));  // open: Output_Display
  Button Reset_System (.out(Reset_System_out));
  Button Reset_RAM (.out(Reset_RAM_out));
  Register_24Bit register_24bit_16 (
    .Load_Store({1'b1, cpu_firmwarechip_1_ram_address_load[0]}), .Input_Data(register_24bit_1_output_data),
    .Clock(and_1_out), .Clear(Reset_System_out), .Output_Data(register_24bit_16_output_data));  // open: Output_Display
  RAM #(.addrWidth(24), .clearpin("true"), .dataWidth(24), .trigger("high"), .\type ("nonvolatile")) ram_1 (
    .addr(register_24bit_16_output_data), .we(cpu_firmwarechip_1_ram_write),
    .oe(cpu_firmwarechip_1_ram_read), .din(register_24bit_1_output_data), .dout(ram_1_dout),
    .clr(Reset_RAM_out));
  assign register_24bit_1_output_data = cpu_firmwarechip_1_enable_ram_output ? ram_1_dout : 24'bz;  // Controlled_Buffer controlled_buffer_1

  // Notes on the sheet:
  //   SP
  //   Z
  //   Y
  //   X
  //   W
  //   V
  //   U
  //   A
  //   B
  //   T
  //   S
  //   R
  //   Q
  //   P
  //   ACC
endmodule

module Register_24Bit (
  input  [23:0] Input_Data,
  input  [1:0] Load_Store,
  input  Clock,
  input  Clear,
  output [23:0] Output_Display,
  output [23:0] Output_Data
);

  Register #(.width(24)) register_1 (.D(Input_Data), .en(Load_Store[0]), .clk(Clock), .Q(Output_Display), .clr(Clear));
  assign Output_Data = Load_Store[1] ? Output_Display : 24'bz;  // Controlled_Buffer controlled_buffer_1
endmodule

module ALU_24Bit (
  input  [23:0] A,
  input  [23:0] B,
  input  [2:0] SelectMode,
  output Flag_Carry,
  output Flag_Zero,
  output [1:0] Flag_Compare,
  output [23:0] ACC
);

  wire adder_1_cout, or_24bit_1_data_out, subtractor_1_bout;
  wire [23:0] adder_1_out, and_1_out, divider_1_out, divider_1_rem, multiplier_1_cout, multiplier_1_out,
       or_1_out, or_2_out, shifter_1_out, subtractor_1_out, xor_1_out;

  Adder #(.width(24)) adder_1 (.a(A), .b(B), .out(adder_1_out), .cout(adder_1_cout));  // open: cin
  Subtractor #(.width(24)) subtractor_1 (.a(A), .b(B), .out(subtractor_1_out), .bout(subtractor_1_bout));  // open: bin
  Multiplier #(.width(24)) multiplier_1 (.a(A), .b(B), .out(multiplier_1_out), .cout(multiplier_1_cout));  // open: cin
  Divider #(.width(24)) divider_1 (.a(A), .b(B), .out(divider_1_out), .rem(divider_1_rem));  // open: upper
  Shifter #(.width(24)) shifter_1 (.in(A), .\dist (B[4:0]), .out(shifter_1_out));
  assign and_1_out = A & B;  // AND_Gate and_1, 24 bits wide
  assign or_1_out = A | B;  // OR_Gate or_1, 24 bits wide
  assign xor_1_out = A ^ B;  // XOR_Gate xor_1, 24 bits wide
  Comparator #(.width(24)) comparator_1 (.a(A), .b(B), .gt(Flag_Compare[0]), .lt(Flag_Compare[1]));  // open: eq
  Or_24Bit or_24bit_1 (.Data_In(or_2_out), .Data_Out(or_24bit_1_data_out));
  assign or_2_out = multiplier_1_cout | divider_1_rem;  // OR_Gate or_2, 24 bits wide
  or or_3 (Flag_Carry, adder_1_cout, subtractor_1_bout, or_24bit_1_data_out);
  Comparator #(.width(24)) comparator_2 (.a(subtractor_1_out), .b({24{1'b0}}), .eq(Flag_Zero));  // open: gt, lt
  Multiplexer #(.select(3), .width(24)) multiplexer_1 (
    .in0(adder_1_out), .in1(subtractor_1_out), .in2(multiplier_1_out), .in3(divider_1_out),
    .in4(shifter_1_out), .in5(and_1_out), .in6(or_1_out), .in7(xor_1_out), .out(ACC), .sel(SelectMode));
endmodule

module CPU_FirmwareChip (
  input  [23:0] Data,
  input  Clock,
  input  Clear,
  input  [1:0] Flag_Compare,
  input  Flag_Zero,
  input  Flag_Carry,
  output [3:0] Source_Register,
  output [3:0] Destination_Register,
  output PC_Enable,
  output RAM_Address_Load,
  output RAM_Read,
  output RAM_Write,
  output [2:0] ExpansionPort_Addreess,
  output ExpansionPort_Store,
  output ExpansionPort_Load,
  output Halt,
  output Instruction_Read,
  output [2:0] ALU_Operation,
  output out_19,
  output Enable_RAM_Output,
  output Enable_Source,
  output [3:0] Register_Address,
  output Register_Load,
  output Register_Store
);

  wire not_1_out, or_1_out;
  wire [0:0] rom_1_data;
  wire [3:0] counter_1_q;
  wire [23:0] register_24bit_1_output_data;

  or or_1 (or_1_out, Clear, Instruction_Read);
  Counter #(.max('hf), .width(4)) counter_1 (
    .clr(or_1_out), .up(1'b1), .count(1'b1), .clk(not_1_out), .Q(counter_1_q));  // open: load, D, carry
  not not_1 (not_1_out, Clock);
  Register_24Bit register_24bit_1 (
    .Load_Store({1'b1, rom_1_data[0]}), .Input_Data(Data), .Clock(Clock), .Clear(Clear),
    .Output_Data({register_24bit_1_output_data[23:16], Destination_Register, Source_Register, register_24bit_1_output_data[7:0]}));  // open: Output_Display
  ROM #(.addrWidth(24), .dataWidth(24)) rom_1 (
    .addr({Flag_Carry, Flag_Zero, Flag_Compare, {8{1'b0}}, register_24bit_1_output_data[7:0], counter_1_q}),
    .data({Register_Store, Register_Load, Register_Address, Enable_Source, Enable_RAM_Output, out_19, ALU_Operation, Instruction_Read, Halt, ExpansionPort_Load, ExpansionPort_Store, ExpansionPort_Addreess, RAM_Write, RAM_Read, RAM_Address_Load, PC_Enable, rom_1_data[0]}));

  // Notes on the sheet:
  //   0-7 opcode
  //   8-11 src register
  //   12-15 dest register
  //   contents of rom_1 (hex, n*v repeats v):
  //   7c0004 1000b 800 13*0 7c0004 1000b 400 800 12*0 7c0004 1000b 820000 800 12*0 7c0004 1000b 7c0004
  //   81000a 800 11*0 7c0004 1000b 7c0004 81000a 800 11*0 7c0004 1000b 7c0004 1000e 20010 800 10*0 7c0004
  //   1000b 7c0004 1000e 100 800 10*0 7c0004 1000b 880000 800 12*0 7c0004 1000b 881000 800 12*0 7c0004
  //   1000b 882000 800 12*0 7c0004 1000b 883000 800 12*0 7c0004 1000b 883000 800 1048396*0 7c0004 1000b
  //   800 13*0 7c0004 1000b 400 800 12*0 7c0004 1000b 820000 800 12*0 7c0004 1000b 7c0004 81000a 800 11*0
  //   7c0004 1000b 7c0004 81000a 800 11*0 7c0004 1000b 7c0004 1000e 20010 800 10*0 7c0004 1000b 7c0004
  //   1000e 100 800 10*0 7c0004 1000b 880000 800 12*0 7c0004 1000b 881000 800 12*0 7c0004 1000b 882000 800
  //   12*0 7c0004 1000b 883000 800 12*0 7c0004 1000b 883000 800 1048396*0 7c0004 1000b 800 13*0 7c0004
  //   1000b 400 800 12*0 7c0004 1000b 820000 800 12*0 7c0004 1000b 7c0004 81000a 800 11*0 7c0004 1000b
  //   7c0004 81000a 800 11*0 7c0004 1000b 7c0004 1000e 20010 800 10*0 7c0004 1000b 7c0004 1000e 100 800
  //   10*0 7c0004 1000b 880000 800 12*0 7c0004 1000b 881000 800 12*0 7c0004 1000b 882000 800 12*0 7c0004
  //   1000b 883000 800 12*0 7c0004 1000b 883000 800 1048396*0 7c0004 1000b 800 13*0 7c0004 1000b 400 800
  //   12*0 7c0004 1000b 820000 800 12*0 7c0004 1000b 7c0004 81000a 800 11*0 7c0004 1000b 7c0004 81000a 800
  //   11*0 7c0004 1000b 7c0004 1000e 20010 800 10*0 7c0004 1000b 7c0004 1000e 100 800 10*0 7c0004 1000b
  //   880000 800 12*0 7c0004 1000b 881000 800 12*0 7c0004 1000b 882000 800 12*0 7c0004 1000b 883000 800
  //   12*0 7c0004 1000b 883000 800 1048396*0 7c0004 1000b 800 13*0 7c0004 1000b 400 800 12*0 7c0004 1000b
  //   820000 800 12*0 7c0004 1000b 7c0004 81000a 800 11*0 7c0004 1000b 7c0004 81000a 800 11*0 7c0004 1000b
  //   7c0004 1000e 20010 800 10*0 7c0004 1000b 7c0004 1000e 100 800 10*0 7c0004 1000b 880000 800 12*0
  //   7c0004 1000b 881000 800 12*0 7c0004 1000b 882000 800 12*0 7c0004 1000b 883000 800 12*0 7c0004 1000b
  //   883000 800 1048396*0 7c0004 1000b 800 13*0 7c0004 1000b 400 800 12*0 7c0004 1000b 820000 800 12*0
  //   7c0004 1000b 7c0004 81000a 800 11*0 7c0004 1000b 7c0004 81000a 800 11*0 7c0004 1000b 7c0004 1000e
  //   20010 800 10*0 7c0004 1000b 7c0004 1000e 100 800 10*0 7c0004 1000b 880000 800 12*0 7c0004 1000b
  //   881000 800 12*0 7c0004 1000b 882000 800 12*0 7c0004 1000b 883000 800 12*0 7c0004 1000b 883000 800
  //   1048396*0 7c0004 1000b 800 13*0 7c0004 1000b 400 800 12*0 7c0004 1000b 820000 800 12*0 7c0004 1000b
  //   7c0004 81000a 800 11*0 7c0004 1000b 7c0004 81000a 800 11*0 7c0004 1000b 7c0004 1000e 20010 800 10*0
  //   7c0004 1000b 7c0004 1000e 100 800 10*0 7c0004 1000b 880000 800 12*0 7c0004 1000b 881000 800 12*0
  //   7c0004 1000b 882000 800 12*0 7c0004 1000b 883000 800 12*0 7c0004 1000b 883000 800 1048396*0 7c0004
  //   1000b 800 13*0 7c0004 1000b 400 800 12*0 7c0004 1000b 820000 800 12*0 7c0004 1000b 7c0004 81000a 800
  //   11*0 7c0004 1000b 7c0004 81000a 800 11*0 7c0004 1000b 7c0004 1000e 20010 800 10*0 7c0004 1000b
  //   7c0004 1000e 100 800 10*0 7c0004 1000b 880000 800 12*0 7c0004 1000b 881000 800 12*0 7c0004 1000b
  //   882000 800 12*0 7c0004 1000b 883000 800 12*0 7c0004 1000b 883000 800 1048396*0 7c0004 1000b 800 13*0
  //   7c0004 1000b 400 800 12*0 7c0004 1000b 820000 800 12*0 7c0004 1000b 7c0004 81000a 800 11*0 7c0004
  //   1000b 7c0004 81000a 800 11*0 7c0004 1000b 7c0004 1000e 20010 800 10*0 7c0004 1000b 7c0004 1000e 100
  //   800 10*0 7c0004 1000b 880000 800 12*0 7c0004 1000b 881000 800 12*0 7c0004 1000b 882000 800 12*0
  //   7c0004 1000b 883000 800 12*0 7c0004 1000b 883000 800 1048396*0 7c0004 1000b 800 13*0 7c0004 1000b
  //   400 800 12*0 7c0004 1000b 820000 800 12*0 7c0004 1000b 7c0004 81000a 800 11*0 7c0004 1000b 7c0004
  //   81000a 800 11*0 7c0004 1000b 7c0004 1000e 20010 800 10*0 7c0004 1000b 7c0004 1000e 100 800 10*0
  //   7c0004 1000b 880000 800 12*0 7c0004 1000b 881000 800 12*0 7c0004 1000b 882000 800 12*0 7c0004 1000b
  //   883000 800 12*0 7c0004 1000b 883000 800 1048396*0 7c0004 1000b 800 13*0 7c0004 1000b 400 800 12*0
  //   7c0004 1000b 820000 800 12*0 7c0004 1000b 7c0004 81000a 800 11*0 7c0004 1000b 7c0004 81000a 800 11*0
  //   7c0004 1000b 7c0004 1000e 20010 800 10*0 7c0004 1000b 7c0004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
endmodule

module Or_24Bit (
  input  [23:0] Data_In,
  output Data_Out
);

  or or_1 (Data_Out, Data_In[0], Data_In[1], Data_In[2], Data_In[3], Data_In[4], Data_In[5], Data_In[6], Data_In[7], Data_In[8], Data_In[9], Data_In[10], Data_In[11], Data_In[12], Data_In[13], Data_In[14], Data_In[15], Data_In[16], Data_In[17], Data_In[18], Data_In[19], Data_In[20], Data_In[21], Data_In[22], Data_In[23]);
endmodule

module Register_Mapper (
  input  [3:0] Source,
  input  Enable_Source,
  input  [3:0] Address,
  input  Load,
  input  Store,
  output [1:0] REA,
  output [1:0] REB,
  output [1:0] ACC,
  output [1:0] REZ,
  output [1:0] REY,
  output [1:0] REX,
  output [1:0] REW,
  output [1:0] REV,
  output [1:0] REU,
  output [1:0] RET,
  output [1:0] RES,
  output [1:0] RER,
  output [1:0] REQ,
  output [1:0] REP,
  output [1:0] SP,
  output [1:0] PC
);

  wire [1:0] demultiplexer_1_out0, demultiplexer_1_out1, demultiplexer_1_out2, demultiplexer_1_out3,
       demultiplexer_1_out4, demultiplexer_1_out5, demultiplexer_1_out6, demultiplexer_1_out7,
       demultiplexer_1_out8, demultiplexer_1_out9, demultiplexer_1_out10, demultiplexer_1_out11,
       demultiplexer_1_out12, demultiplexer_1_out13, demultiplexer_1_out14, demultiplexer_1_out15,
       demultiplexer_2_out0, demultiplexer_2_out1, demultiplexer_2_out2, demultiplexer_2_out3,
       demultiplexer_2_out4, demultiplexer_2_out5, demultiplexer_2_out6, demultiplexer_2_out7,
       demultiplexer_2_out8, demultiplexer_2_out9, demultiplexer_2_out10, demultiplexer_2_out11,
       demultiplexer_2_out12, demultiplexer_2_out13, demultiplexer_2_out14, demultiplexer_2_out15,
       multiplexer_1_out;

  Multiplexer #(.width(2)) multiplexer_1 (.in0(2'b00), .in1(2'b10), .out(multiplexer_1_out), .sel(Enable_Source));
  Demultiplexer #(.select(4), .width(2)) demultiplexer_1 (
    .out0(demultiplexer_1_out0), .out1(demultiplexer_1_out1), .out2(demultiplexer_1_out2),
    .out3(demultiplexer_1_out3), .out4(demultiplexer_1_out4), .out5(demultiplexer_1_out5),
    .out6(demultiplexer_1_out6), .out7(demultiplexer_1_out7), .out8(demultiplexer_1_out8),
    .out9(demultiplexer_1_out9), .out10(demultiplexer_1_out10), .out11(demultiplexer_1_out11),
    .out12(demultiplexer_1_out12), .out13(demultiplexer_1_out13), .out14(demultiplexer_1_out14),
    .out15(demultiplexer_1_out15), .in(multiplexer_1_out), .sel(Source));
  Demultiplexer #(.select(4), .width(2)) demultiplexer_2 (
    .out0(demultiplexer_2_out0), .out1(demultiplexer_2_out1), .out2(demultiplexer_2_out2),
    .out3(demultiplexer_2_out3), .out4(demultiplexer_2_out4), .out5(demultiplexer_2_out5),
    .out6(demultiplexer_2_out6), .out7(demultiplexer_2_out7), .out8(demultiplexer_2_out8),
    .out9(demultiplexer_2_out9), .out10(demultiplexer_2_out10), .out11(demultiplexer_2_out11),
    .out12(demultiplexer_2_out12), .out13(demultiplexer_2_out13), .out14(demultiplexer_2_out14),
    .out15(demultiplexer_2_out15), .in({Load, Store}), .sel(Address));
  assign REA = demultiplexer_1_out0 | demultiplexer_2_out0;  // OR_Gate or_1, 2 bits wide
  assign REB = demultiplexer_1_out1 | demultiplexer_2_out1;  // OR_Gate or_2, 2 bits wide
  assign ACC = demultiplexer_1_out2 | demultiplexer_2_out2;  // OR_Gate or_3, 2 bits wide
  assign REZ = demultiplexer_1_out3 | demultiplexer_2_out3;  // OR_Gate or_4, 2 bits wide
  assign REY = demultiplexer_1_out4 | demultiplexer_2_out4;  // OR_Gate or_5, 2 bits wide
  assign REX = demultiplexer_1_out5 | demultiplexer_2_out5;  // OR_Gate or_6, 2 bits wide
  assign REW = demultiplexer_1_out6 | demultiplexer_2_out6;  // OR_Gate or_7, 2 bits wide
  assign REV = demultiplexer_1_out7 | demultiplexer_2_out7;  // OR_Gate or_8, 2 bits wide
  assign REU = demultiplexer_1_out8 | demultiplexer_2_out8;  // OR_Gate or_9, 2 bits wide
  assign RET = demultiplexer_1_out9 | demultiplexer_2_out9;  // OR_Gate or_10, 2 bits wide
  assign RES = demultiplexer_1_out10 | demultiplexer_2_out10;  // OR_Gate or_11, 2 bits wide
  assign RER = demultiplexer_1_out11 | demultiplexer_2_out11;  // OR_Gate or_12, 2 bits wide
  assign REQ = demultiplexer_1_out12 | demultiplexer_2_out12;  // OR_Gate or_13, 2 bits wide
  assign REP = demultiplexer_1_out13 | demultiplexer_2_out13;  // OR_Gate or_14, 2 bits wide
  assign SP = demultiplexer_1_out14 | demultiplexer_2_out14;  // OR_Gate or_15, 2 bits wide
  assign PC = demultiplexer_1_out15 | demultiplexer_2_out15;  // OR_Gate or_16, 2 bits wide
endmodule

module Decoder_4Bit (
  input  [3:0] Data,
  output O_F,
  output O_E,
  output O_D,
  output O_C,
  output O_B,
  output O_A,
  output O_9,
  output O_8,
  output O_7,
  output O_6,
  output O_5,
  output O_4,
  output O_3,
  output O_2,
  output O_1,
  output O_0
);

  wire not_1_out, not_2_out, not_3_out, not_4_out;

  not not_1 (not_1_out, Data[3]);
  not not_2 (not_2_out, Data[2]);
  not not_3 (not_3_out, Data[1]);
  not not_4 (not_4_out, Data[0]);
  and and_1 (O_0, not_1_out, not_2_out, not_3_out, not_4_out);
  and and_2 (O_1, not_1_out, not_2_out, not_3_out, Data[0]);
  and and_3 (O_2, not_1_out, not_2_out, Data[1], not_4_out);
  and and_4 (O_3, not_1_out, not_2_out, Data[1], Data[0]);
  and and_5 (O_4, not_1_out, Data[2], not_3_out, not_4_out);
  and and_6 (O_5, not_1_out, Data[2], not_3_out, Data[0]);
  and and_7 (O_6, not_1_out, Data[2], Data[1], not_4_out);
  and and_8 (O_7, not_1_out, Data[2], Data[1], Data[0]);
  and and_9 (O_8, Data[3], not_2_out, not_3_out, not_4_out);
  and and_10 (O_9, Data[3], not_2_out, not_3_out, Data[0]);
  and and_11 (O_A, Data[3], not_2_out, Data[1], not_4_out);
  and and_12 (O_B, Data[3], not_2_out, Data[1], Data[0]);
  and and_13 (O_C, Data[3], Data[2], not_3_out, not_4_out);
  and and_14 (O_D, Data[3], Data[2], not_3_out, Data[0]);
  and and_15 (O_E, Data[3], Data[2], Data[1], not_4_out);
  and and_16 (O_F, Data[3], Data[2], Data[1], Data[0]);
endmodule

module ProgramCounter_24Bit (
  input  Clear,
  input  [1:0] Load,
  input  Enable,
  input  Clock,
  input  [23:0] Data,
  output [23:0] Pointer
);

  wire [23:0] counter_1_q;

  Counter #(.max('hffffff), .width(24)) counter_1 (
    .clr(Clear), .load(Load[0]), .count(Enable), .clk(Clock), .D(Data), .Q(counter_1_q));  // open: up, carry
  assign Pointer = Load[1] ? counter_1_q : 24'bz;  // Controlled_Buffer controlled_buffer_1
endmodule

module Expansion_Mapper (
  input  [2:0] ExpansionPort_Address,
  input  Store,
  input  Load,
  output [1:0] EP0,
  output [1:0] EP1,
  output [1:0] EP2,
  output [1:0] EP3,
  output [1:0] EP4,
  output [1:0] EP5,
  output [1:0] EP6,
  output [1:0] EP7
);

  Demultiplexer #(.select(3), .width(2)) demultiplexer_1 (
    .out0(EP0), .out1(EP1), .out2(EP2), .out3(EP3), .out4(EP4), .out5(EP5), .out6(EP6), .out7(EP7),
    .in({Load, Store}), .sel(ExpansionPort_Address));
endmodule
